// Logisim project aialu.circ as structural Verilog
module Full_Adder (
  input  A,
  input  B,
  input  C,
  output out_4,
  output out_5
);

  wire and_1_out, and_2_out, xor_1_out;

  xor xor_1 (xor_1_out, A, B);
  xor xor_2 (out_4, xor_1_out, C);
  and and_1 (and_1_out, C, xor_1_out);
  and and_2 (and_2_out, B, A);
  or or_1 (out_5, and_1_out, and_2_out);
endmodule

module Half_Adder (
  input  A,
  input  B,
  output out_3,
  output out_4
);

  xor xor_1 (out_3, A, B);
  and and_1 (out_4, A, B);
endmodule
