// Logisim project s1.circ as structural Verilog
module Half_Adder (
  input  A,
  input  B,
  output Somma,
  output Riporto
);

  xor xor_1 (Somma, A, B);
  and and_1 (Riporto, A, B);
endmodule

module Full_Adder (
  input  A,
  input  B,
  input  C,
  output Somma,
  output Riporto
);

  wire and_1_out, and_2_out, and_3_out, xor_1_out;

  xor xor_1 (xor_1_out, A, B);
  and and_1 (and_1_out, A, C);
  and and_2 (and_2_out, A, B);
  and and_3 (and_3_out, B, C);
  xor xor_2 (Somma, xor_1_out, C);
  or or_1 (Riporto, and_1_out, and_2_out, and_3_out);
endmodule

module sommatore_8 (
  input  [7:0] A,
  input  [7:0] B,
  input  Enable,
  input  in_4,
  output [7:0] out_5,
  output overflow
);

  wire c1, c2, c3, c4, c5, c6, c7, not_1_out, s1, s2, s3, s4, s5, s6, s7, s8;

  Full_Adder full_adder_1 (.Somma(s1), .Riporto(c1), .A(A[0]), .B(B[0]), .C(in_4));
  Full_Adder full_adder_2 (.Somma(s8), .Riporto(overflow), .A(A[7]), .B(B[7]), .C(c7));
  Full_Adder full_adder_3 (.Somma(s7), .Riporto(c7), .A(A[6]), .B(B[6]), .C(c6));
  Full_Adder full_adder_4 (.Somma(s2), .Riporto(c2), .A(A[1]), .B(B[1]), .C(c1));
  Full_Adder full_adder_5 (.Somma(s3), .Riporto(c3), .A(A[2]), .B(B[2]), .C(c2));
  Full_Adder full_adder_6 (.Somma(s4), .Riporto(c4), .A(A[3]), .B(B[3]), .C(c3));
  Full_Adder full_adder_7 (.Somma(s5), .Riporto(c5), .A(A[4]), .B(B[4]), .C(c4));
  Full_Adder full_adder_8 (.Somma(s6), .Riporto(c6), .A(A[5]), .B(B[5]), .C(c5));
  not not_1 (not_1_out, Enable);
  and and_1 (out_5[0], s1, not_1_out);
  and and_2 (out_5[1], s2, not_1_out);
  and and_3 (out_5[2], s3, not_1_out);
  and and_4 (out_5[3], s4, not_1_out);
  and and_5 (out_5[4], s5, not_1_out);
  and and_6 (out_5[5], s6, not_1_out);
  and and_7 (out_5[6], s7, not_1_out);
  and and_8 (out_5[7], s8, not_1_out);

  // Other names for the same wires on the sheet: a_t = A[1]; c = A[2]; e = A[3]; g = A[4]; i = A[5]; m = A[6];
  //   o = A[7]; b_t = B[1]; d = B[2]; f = B[3]; h = B[4]; l = B[5]; n = B[6]; p = B[7]
endmodule

module sottrattore_8 (
  input  [7:0] A,
  input  [7:0] B,
  input  Enable,
  output [7:0] out_4,
  output Overflow
);

  wire and_1_out, b_t, c1, c2, c3, c4, c5, c6, c7, d, f, h, l, n, p, s1, s2, s3, s4, s5, s6, s7, s8,
       xnor_1_out;
  wire [0:0] not_1_out;

  // Probe on A
  // Probe on B
  Full_Adder full_adder_1 (.Somma(s1), .Riporto(c1), .A(A[0]), .B(not_1_out[0]), .C(1'b1));
  Full_Adder full_adder_2 (.Somma(s8), .A(A[7]), .B(p), .C(c7));  // open: Riporto
  xnor xnor_1 (xnor_1_out, A[7], p);
  assign {p, n, l, h, f, d, b_t, not_1_out[0]} = ~B;  // NOT_Gate not_1, 8 bits wide
  and and_1 (and_1_out, xnor_1_out, p, A[7]);
  Full_Adder full_adder_3 (.Somma(s7), .Riporto(c7), .A(A[6]), .B(n), .C(c6));
  and and_2 (Overflow, and_1_out, c7);
  Full_Adder full_adder_4 (.Somma(s2), .Riporto(c2), .A(A[1]), .B(b_t), .C(c1));
  Full_Adder full_adder_5 (.Somma(s3), .Riporto(c3), .A(A[2]), .B(d), .C(c2));
  Full_Adder full_adder_6 (.Somma(s4), .Riporto(c4), .A(A[3]), .B(f), .C(c3));
  Full_Adder full_adder_7 (.Somma(s5), .Riporto(c5), .A(A[4]), .B(h), .C(c4));
  Full_Adder full_adder_8 (.Somma(s6), .Riporto(c6), .A(A[5]), .B(l), .C(c5));
  and and_3 (out_4[0], s1, Enable);
  and and_4 (out_4[1], s2, Enable);
  and and_5 (out_4[2], s3, Enable);
  and and_6 (out_4[3], s4, Enable);
  and and_7 (out_4[4], s5, Enable);
  and and_8 (out_4[5], s6, Enable);
  and and_9 (out_4[6], s7, Enable);
  and and_10 (out_4[7], s8, Enable);
  // Probe on out_4

  // Other names for the same wires on the sheet: a_t = A[1]; c = A[2]; e = A[3]; g = A[4]; i = A[5]; m = A[6];
  //   o = A[7]
endmodule

module AiArith (
  input  [7:0] A,
  input  [7:0] B,
  input  Enable,
  input  in_4,
  output [7:0] out_5,
  output out_6
);

  wire sommatore_8_1_overflow, sottrattore_8_1_overflow;
  wire [7:0] sommatore_8_1_out_5, sottrattore_8_1_out_4;

  sottrattore_8 sottrattore_8_1 (
    .out_4(sottrattore_8_1_out_4), .A(A), .B(B), .Enable(Enable), .Overflow(sottrattore_8_1_overflow));
  sommatore_8 sommatore_8_1 (
    .out_5(sommatore_8_1_out_5), .overflow(sommatore_8_1_overflow), .A(A), .B(B), .Enable(Enable), .in_4(in_4));
  or or_1 (out_6, sottrattore_8_1_overflow, sommatore_8_1_overflow);
  assign out_5 = sottrattore_8_1_out_4 | sommatore_8_1_out_5;  // OR_Gate or_2, 8 bits wide
endmodule

module AiArith2 (
  input  [7:0] A,
  input  in_2,
  input  [7:0] B,
  input  _0____1,
  output [7:0] out_5,
  output out_6
);

  AiArith aiarith_1 (.Enable(_0____1), .out_5(out_5), .A(A), .B(B), .in_4(in_2), .out_6(out_6));
endmodule

module Mux_8bit (
  input  S0,
  input  S1,
  input  S2,
  input  D0,
  input  D1,
  input  D2,
  input  D3,
  input  D4,
  input  D5,
  input  D6,
  input  D7,
  output out_12
);

  wire and_1_out, and_2_out, and_3_out, and_4_out, and_5_out, and_6_out, and_7_out, and_8_out, not_1_out,
       not_2_out, not_3_out;

  not not_1 (not_1_out, S0);
  not not_2 (not_2_out, S2);
  not not_3 (not_3_out, S1);
  and and_1 (and_1_out, not_1_out, not_3_out, not_2_out, D0);
  and and_2 (and_2_out, not_1_out, not_3_out, S2, D1);
  and and_3 (and_3_out, not_1_out, S1, not_2_out, D2);
  and and_4 (and_4_out, not_1_out, S1, S2, D3);
  and and_5 (and_5_out, S0, not_3_out, not_2_out, D4);
  and and_6 (and_6_out, S0, not_3_out, S2, D5);
  and and_7 (and_7_out, S0, S1, not_2_out, D6);
  and and_8 (and_8_out, S0, S1, S2, D7);
  or or_1 (out_12, and_1_out, and_2_out, and_3_out, and_4_out, and_5_out, and_6_out, and_7_out, and_8_out);
endmodule
